// Logisim project capstone.circ as structural Verilog: 1 circuit, main circuit main
module main (
);

  wire ADD_PAGE, and_1_out, and_3_out, buffer_31_out, CARRY_FLAG, CARRY_FLAG_TRUE, CLK, comparator_1_gt,
       comparator_2_gt, comparator_3_eq, comparator_4_eq, comparator_5_eq, comparator_6_eq, COND_INS,
       demultiplexer_1_out1, demultiplexer_1_out2, demultiplexer_1_out3, demultiplexer_1_out4,
       demultiplexer_1_out5, demultiplexer_1_out6, demultiplexer_2_out1, demultiplexer_2_out2,
       demultiplexer_2_out3, demultiplexer_2_out4, demultiplexer_2_out5, demultiplexer_2_out6,
       demultiplexer_2_out7, demultiplexer_4_out1, demultiplexer_4_out2, demultiplexer_4_out3,
       demultiplexer_5_out1, demultiplexer_5_out2, demultiplexer_5_out3, demultiplexer_5_out4,
       demultiplexer_5_out5, demultiplexer_5_out6, EDI, INC_PC, INC_SP, LOAD_PC, MODE_SP, multiplexer_5_out,
       NEGATIVE_FLAG_TRUE, not_2_out, not_3_out, not_4_out, or_5_out, or_7_out, OUT_MODE, OVERFLOW,
       OVERFLOW_FLAG_TRUE, PARITY_FLAG_TRUE, PAUSE_PC, pull_resistor_5_node, pull_resistor_6_node, READ_A,
       READ_ALU_ADD, READ_ALU_AND, READ_ALU_DECP, READ_ALU_INCA, READ_ALU_INCP, READ_ALU_INCX, READ_ALU_INCY,
       READ_ALU_LSL, READ_ALU_LSR, READ_ALU_NOT, READ_ALU_OR, READ_ALU_RL, READ_ALU_RR, READ_ALU_SUB, READ_I,
       READ_MAR, READ_MEM, READ_P, READ_SP, READ_X, READ_Y, RESET_PC, SUB_PAGE, WRITE_A, WRITE_I, WRITE_MAR,
       WRITE_MEM, WRITE_P, WRITE_X, WRITE_Y, ZERO_FLAG_TRUE;
  wire [3:0] controlled_buffer_1_out_2, Instruction_Register_q_2;
  wire [4:0] FLAG_REG_IN, FLAG_REG_INS, FLAG_REG_OUT, or_2_out, or_3_out, pull_resistor_7_node,
       pull_resistor_8_node, pull_resistor_9_node, pull_resistor_10_node;
  wire [7:0] STACK_PTR_q;
  wire [10:0] INS_Step_Counter_q, MI_STRING;
  wire [11:0] controlled_buffer_1_out, Instruction_Register_q;
  wire [15:0] ACC, adder_1_out, adder_2_out, adder_3_out, adder_4_out, adder_5_out, adder_6_out, adder_8_out,
       ALU_RES, and_2_out, bit_extender_1_out, buffer_9_out, controlled_buffer_2_out,
       controlled_buffer_3_out, controlled_buffer_4_out, CURR_ADD, DATA_BUS_IN, DATA_BUS_OUT, INS_DECODER,
       INS_Lookup_Table_data, INS_REG, Memory_Address_Register_q, multiplexer_1_out, multiplexer_2_out,
       multiplexer_3_out, multiplexer_4_out, multiplexer_6_out, not_1_out, or_1_out, P, P_ADDRESS,
       Program_Counter_q, ram_1_dout, shifter_1_out, shifter_2_out, shifter_3_out, shifter_4_out,
       subtractor_1_out, subtractor_2_out, subtractor_3_out, X, Y;
  wire [15:5] buffer_8_out;

  Clock clock_1 (.out(CLK));
  // Probe on DATA_BUS_IN
  // Probe on INS_REG
  // Probe on DATA_BUS_OUT
  // Probe on ALU_RES
  Multiplexer #(.width(16)) multiplexer_1 (
    .in0(DATA_BUS_IN), .in1(DATA_BUS_OUT), .out(multiplexer_1_out), .sel(OUT_MODE));
  Multiplexer #(.width(16)) multiplexer_2 (
    .in0(DATA_BUS_IN), .in1(DATA_BUS_OUT), .out(multiplexer_2_out), .sel(OUT_MODE));
  Multiplexer #(.width(16)) multiplexer_3 (
    .in0(DATA_BUS_IN), .in1(DATA_BUS_OUT), .out(multiplexer_3_out), .sel(OUT_MODE));
  Multiplexer #(.width(16)) multiplexer_4 (
    .in0(DATA_BUS_IN), .in1(DATA_BUS_OUT), .out(multiplexer_4_out), .sel(OUT_MODE));
  Comparator #(.width(11)) comparator_1 (.a(MI_STRING), .b({11{1'b0}}), .gt(comparator_1_gt));  // open: eq, lt
  // Probe on ACC
  Register #(.width(16)) X_Register (.D(multiplexer_1_out), .en(WRITE_X), .clk(CLK), .Q(X));  // open: clr
  Register #(.width(16)) Y_Register (.D(multiplexer_2_out), .en(WRITE_Y), .clk(CLK), .Q(Y));  // open: clr
  Register #(.width(16)) Accumulator (.D(multiplexer_3_out), .en(WRITE_A), .clk(CLK), .Q(ACC));  // open: clr
  Register #(.width(16)) Page_Register (.D(multiplexer_4_out), .en(WRITE_P), .clk(CLK), .Q(P));  // open: clr
  Register #(.width(16)) Instruction_Register (
    .D(INS_REG), .en(EDI), .clk(CLK), .Q({Instruction_Register_q_2, Instruction_Register_q}), .clr(and_1_out));
  and and_1 (and_1_out, EDI, comparator_1_gt);
  // Probe on DATA_BUS_IN
  // Probe on P
  // Probe on P
  // Probe on P_ADDRESS
  // Probe on CURR_ADD
  Hex_Digit_Display hex_digit_display_1 (.value(controlled_buffer_1_out_2));  // open: dp
  assign {controlled_buffer_1_out_2, controlled_buffer_1_out} = READ_X ? X : 16'bz;  // Controlled_Buffer controlled_buffer_1
  assign controlled_buffer_2_out = READ_Y ? Y : 16'bz;  // Controlled_Buffer controlled_buffer_2
  assign controlled_buffer_3_out = READ_A ? ACC : 16'bz;  // Controlled_Buffer controlled_buffer_3
  Multiplier #(.width(16)) multiplier_1 (.a(P), .b(16'hff), .out(P_ADDRESS));  // open: cin, cout
  assign {FLAG_REG_OUT[4:2], CARRY_FLAG, FLAG_REG_OUT[0]} = FLAG_REG_IN;  // Buffer buffer_1, 5 bits wide
  assign not_1_out = ~ACC;  // NOT_Gate not_1, 16 bits wide
  Shifter #(.width(16)) shifter_1 (.in(ACC), .\dist (4'b0001), .out(shifter_1_out));
  Shifter #(.shift("lr"), .width(16)) shifter_2 (.in(ACC), .\dist (4'b0001), .out(shifter_2_out));
  Shifter #(.shift("rl"), .width(16)) shifter_3 (.in(ACC), .\dist (4'b0001), .out(shifter_3_out));
  Shifter #(.shift("rr"), .width(16)) shifter_4 (.in(ACC), .\dist (4'b0001), .out(shifter_4_out));
  Subtractor #(.width(16)) subtractor_1 (.a(ACC), .b(DATA_BUS_IN), .out(subtractor_1_out));  // open: bin, bout
  Adder #(.width(16)) adder_1 (.a(ACC), .b(16'h1), .out(adder_1_out));  // open: cin, cout
  Adder #(.width(16)) adder_2 (.a(X), .b(16'h1), .out(adder_2_out));  // open: cin, cout
  Adder #(.width(16)) adder_3 (.a(Y), .b(16'h1), .out(adder_3_out));  // open: cin, cout
  Adder #(.width(16)) adder_4 (.a(P), .b(16'h1), .out(adder_4_out));  // open: cin, cout
  Subtractor #(.width(16)) subtractor_2 (.a(P), .b(16'h1), .out(subtractor_2_out));  // open: bin, bout
  Adder #(.width(16)) adder_5 (.a(P_ADDRESS), .b(CURR_ADD), .out(adder_5_out));  // open: cin, cout
  Subtractor #(.width(16)) subtractor_3 (.a(CURR_ADD), .b(P_ADDRESS), .out(subtractor_3_out));  // open: bin, bout
  Pull_Resistor pull_resistor_1 (.node(DATA_BUS_IN));
  Pull_Resistor pull_resistor_2 (.node(INS_REG));
  Pull_Resistor pull_resistor_3 (.node(DATA_BUS_OUT));
  Pull_Resistor pull_resistor_4 (.node(ALU_RES));
  Hex_Digit_Display hex_digit_display_2 (.value(controlled_buffer_1_out[11:8]));  // open: dp
  Hex_Digit_Display hex_digit_display_3 (.value(controlled_buffer_1_out[7:4]));  // open: dp
  assign DATA_BUS_OUT = {controlled_buffer_1_out_2, controlled_buffer_1_out};  // Buffer buffer_2, 16 bits wide
  assign DATA_BUS_OUT = controlled_buffer_2_out;  // Buffer buffer_3, 16 bits wide
  assign controlled_buffer_4_out = READ_P ? P_ADDRESS : 16'bz;  // Controlled_Buffer controlled_buffer_4
  Hex_Digit_Display hex_digit_display_4 (.value(Instruction_Register_q_2));  // open: dp
  assign and_2_out = ACC & DATA_BUS_IN;  // AND_Gate and_2, 16 bits wide
  assign DATA_BUS_OUT = READ_ALU_AND ? and_2_out : 16'bz;  // Controlled_Buffer controlled_buffer_5
  // Probe on or_1_out
  assign or_1_out = ACC | DATA_BUS_IN;  // OR_Gate or_1, 16 bits wide
  assign DATA_BUS_OUT = READ_ALU_OR ? or_1_out : 16'bz;  // Controlled_Buffer controlled_buffer_6
  assign DATA_BUS_OUT = READ_ALU_NOT ? not_1_out : 16'bz;  // Controlled_Buffer controlled_buffer_7
  assign DATA_BUS_OUT = READ_ALU_LSL ? shifter_1_out : 16'bz;  // Controlled_Buffer controlled_buffer_8
  assign DATA_BUS_OUT = READ_ALU_LSR ? shifter_2_out : 16'bz;  // Controlled_Buffer controlled_buffer_9
  assign DATA_BUS_OUT = READ_ALU_RL ? shifter_3_out : 16'bz;  // Controlled_Buffer controlled_buffer_10
  assign DATA_BUS_OUT = READ_ALU_RR ? shifter_4_out : 16'bz;  // Controlled_Buffer controlled_buffer_11
  Adder #(.width(16)) adder_6 (.a(ACC), .b(DATA_BUS_IN), .out(adder_6_out), .cout(OVERFLOW));  // open: cin
  assign DATA_BUS_OUT = READ_ALU_SUB ? subtractor_1_out : 16'bz;  // Controlled_Buffer controlled_buffer_12
  assign DATA_BUS_OUT = READ_ALU_INCA ? adder_1_out : 16'bz;  // Controlled_Buffer controlled_buffer_13
  assign DATA_BUS_OUT = READ_ALU_INCX ? adder_2_out : 16'bz;  // Controlled_Buffer controlled_buffer_14
  assign DATA_BUS_OUT = READ_ALU_INCY ? adder_3_out : 16'bz;  // Controlled_Buffer controlled_buffer_15
  assign DATA_BUS_OUT = READ_ALU_INCP ? adder_4_out : 16'bz;  // Controlled_Buffer controlled_buffer_16
  // Probe on DATA_BUS_OUT
  assign DATA_BUS_OUT = READ_ALU_DECP ? subtractor_2_out : 16'bz;  // Controlled_Buffer controlled_buffer_17
  // Probe on DATA_BUS_OUT
  assign DATA_BUS_OUT = ADD_PAGE ? adder_5_out : 16'bz;  // Controlled_Buffer controlled_buffer_18
  assign DATA_BUS_OUT = SUB_PAGE ? subtractor_3_out : 16'bz;  // Controlled_Buffer controlled_buffer_19
  // Probe on DATA_BUS_OUT
  Hex_Digit_Display hex_digit_display_5 (.value(controlled_buffer_1_out[3:0]));  // open: dp
  // Probe on ACC
  assign DATA_BUS_OUT = controlled_buffer_3_out;  // Buffer buffer_4, 16 bits wide
  assign DATA_BUS_OUT = controlled_buffer_4_out;  // Buffer buffer_5, 16 bits wide
  Hex_Digit_Display hex_digit_display_6 (.value(Instruction_Register_q[11:8]));  // open: dp
  Hex_Digit_Display hex_digit_display_7 (.value(Instruction_Register_q[7:4]));  // open: dp
  assign INS_DECODER = {Instruction_Register_q_2, Instruction_Register_q};  // Buffer buffer_6, 16 bits wide
  // Probe on INS_DECODER
  // Probe on ALU_RES
  // Probe on DATA_BUS_OUT
  // Probe on DATA_BUS_IN
  // Probe on DATA_BUS_OUT
  assign DATA_BUS_OUT = READ_ALU_ADD ? adder_6_out : 16'bz;  // Controlled_Buffer controlled_buffer_20
  // Probe on adder_6_out
  // Probe on DATA_BUS_OUT
  Hex_Digit_Display hex_digit_display_8 (.value(Instruction_Register_q[3:0]));  // open: dp
  Comparator #(.width(16)) comparator_2 (.a(INS_DECODER), .b({16{1'b0}}), .gt(comparator_2_gt));  // open: eq, lt
  // Probe on DATA_BUS_OUT
  Counter #(.max('h7ff), .width(11)) INS_Step_Counter (
    .clr(EDI), .clk(and_3_out), .D(11'h1), .Q(INS_Step_Counter_q));  // open: load, up, count, carry
  and and_3 (and_3_out, CLK, comparator_2_gt);
  Pull_Resistor pull_resistor_5 (.node(pull_resistor_5_node));
  assign pull_resistor_5_node = FLAG_REG_OUT[0] ? LOAD_PC : 1'bz;  // Controlled_Buffer controlled_buffer_21
  Multiplexer multiplexer_5 (.in0(LOAD_PC), .in1(pull_resistor_5_node), .out(multiplexer_5_out), .sel(COND_INS));
  // Probe on multiplexer_5_out
  Pull_Resistor pull_resistor_6 (.node(pull_resistor_6_node));
  assign pull_resistor_6_node = not_2_out ? OUT_MODE : 1'bz;  // Controlled_Buffer controlled_buffer_22
  not not_2 (not_2_out, COND_INS);
  buf buffer_7 (INC_PC, CLK);
  // Probe on DATA_BUS_OUT
  Counter #(.max('hffff), .trigger("falling"), .width(16)) Program_Counter (
    .clr(RESET_PC), .load(multiplexer_5_out), .clk(INC_PC), .D(multiplexer_6_out), .Q(Program_Counter_q));  // open: up, count, carry
  Multiplexer #(.width(16)) multiplexer_6 (
    .in0(DATA_BUS_IN), .in1(DATA_BUS_OUT), .out(multiplexer_6_out), .sel(pull_resistor_6_node));
  assign {buffer_8_out, FLAG_REG_INS} = INS_DECODER;  // Buffer buffer_8, 16 bits wide
  // Probe on buffer_8_out
  assign buffer_9_out = DATA_BUS_OUT;  // Buffer buffer_9, 16 bits wide
  Counter STACK_PTR (.up(not_3_out), .clk(INC_SP), .D(8'h1), .Q(STACK_PTR_q));  // open: clr, load, count, carry
  not not_3 (not_3_out, MODE_SP);
  // Probe on FLAG_REG_INS
  Adder #(.width(11)) adder_7 (.a(buffer_8_out), .b(INS_Step_Counter_q), .out(MI_STRING));  // open: cin, cout
  Comparator #(.width(16)) comparator_3 (.a({16{1'b0}}), .b(buffer_9_out), .eq(comparator_3_eq));  // open: gt, lt
  Pull_Resistor pull_resistor_7 (.node(pull_resistor_7_node));
  assign pull_resistor_7_node = buffer_9_out[0] ? 5'b01000 : 5'bz;  // Controlled_Buffer controlled_buffer_23
  Pull_Resistor pull_resistor_8 (.node(pull_resistor_8_node));
  assign pull_resistor_8_node = buffer_9_out[15] ? 5'b10000 : 5'bz;  // Controlled_Buffer controlled_buffer_24
  // Probe on {NEGATIVE_FLAG_TRUE, PARITY_FLAG_TRUE, OVERFLOW_FLAG_TRUE, CARRY_FLAG_TRUE, ZERO_FLAG_TRUE}
  assign {NEGATIVE_FLAG_TRUE, PARITY_FLAG_TRUE, OVERFLOW_FLAG_TRUE, CARRY_FLAG_TRUE, ZERO_FLAG_TRUE} = FLAG_REG_INS & {FLAG_REG_OUT[4:2], CARRY_FLAG, FLAG_REG_OUT[0]};  // AND_Gate and_4, 5 bits wide
  // Probe on CURR_ADD
  assign CURR_ADD = Program_Counter_q;  // Buffer buffer_10, 16 bits wide
  ROM #(.addrWidth(11), .dataWidth(16)) INS_Lookup_Table (
    .addr(MI_STRING), .data({INS_Lookup_Table_data[15:5], EDI, INS_Lookup_Table_data[3:0]}));
  Pull_Resistor pull_resistor_9 (.node(pull_resistor_9_node));
  assign pull_resistor_9_node = comparator_3_eq ? 5'b00001 : 5'bz;  // Controlled_Buffer controlled_buffer_25
  assign or_2_out = pull_resistor_7_node | pull_resistor_8_node;  // OR_Gate or_2, 5 bits wide
  Adder #(.width(16)) adder_8 (.a(16'h1), .b(Program_Counter_q), .out(adder_8_out));  // open: cin, cout
  // Probe on Program_Counter_q
  Pull_Resistor pull_resistor_10 (.node(pull_resistor_10_node));
  assign pull_resistor_10_node = OVERFLOW ? 5'b00100 : 5'bz;  // Controlled_Buffer controlled_buffer_26
  Register #(.width(16)) Memory_Address_Register (
    .D(adder_8_out), .en(WRITE_MAR), .clk(CLK), .Q(Memory_Address_Register_q));  // open: clr
  // Probe on bit_extender_1_out
  assign bit_extender_1_out = {{8{1'b0}}, STACK_PTR_q};  // Bit_Extender bit_extender_1
  // Probe on or_3_out
  assign or_3_out = pull_resistor_9_node | or_2_out;  // OR_Gate or_3, 5 bits wide
  assign FLAG_REG_IN = pull_resistor_10_node | or_3_out;  // OR_Gate or_4, 5 bits wide
  not not_4 (not_4_out, WRITE_MEM);
  assign DATA_BUS_OUT = READ_SP ? bit_extender_1_out : 16'bz;  // Controlled_Buffer controlled_buffer_27
  // Probe on INS_Lookup_Table_data[12:10]
  // Probe on INS_Lookup_Table_data[15:13]
  Demultiplexer #(.select(3)) demultiplexer_1 (
    .out1(demultiplexer_1_out1), .out2(demultiplexer_1_out2), .out3(demultiplexer_1_out3),
    .out4(demultiplexer_1_out4), .out5(demultiplexer_1_out5), .out6(demultiplexer_1_out6), .in(1'b1),
    .sel(INS_Lookup_Table_data[15:13]));  // open: out0, out7
  // Probe on or_3_out
  assign DATA_BUS_OUT = READ_MAR ? Memory_Address_Register_q : 16'bz;  // Controlled_Buffer controlled_buffer_28
  RAM #(.addrWidth(16), .dataWidth(16)) ram_1 (
    .addr(Program_Counter_q), .we(WRITE_MEM), .oe(or_5_out), .clk(CLK), .din(DATA_BUS_OUT), .dout(ram_1_dout));
  or or_5 (or_5_out, READ_MEM, not_4_out);
  // Probe on INS_Lookup_Table_data[6:5]
  // Probe on INS_Lookup_Table_data[9:7]
  Demultiplexer #(.select(3)) demultiplexer_2 (
    .out1(demultiplexer_2_out1), .out2(demultiplexer_2_out2), .out3(demultiplexer_2_out3),
    .out4(demultiplexer_2_out4), .out5(demultiplexer_2_out5), .out6(demultiplexer_2_out6),
    .out7(demultiplexer_2_out7), .in(1'b1), .sel(INS_Lookup_Table_data[12:10]));  // open: out0
  buf buffer_11 (WRITE_X, demultiplexer_1_out1);
  buf buffer_12 (WRITE_Y, demultiplexer_1_out2);
  buf buffer_13 (WRITE_A, demultiplexer_1_out3);
  buf buffer_14 (WRITE_P, demultiplexer_1_out4);
  buf buffer_15 (WRITE_I, demultiplexer_1_out5);
  buf buffer_16 (WRITE_MEM, demultiplexer_1_out6);
  // Probe on DATA_BUS_OUT
  Demultiplexer #(.select(4)) demultiplexer_3 (
    .out1(READ_ALU_AND), .out2(READ_ALU_OR), .out3(READ_ALU_LSL), .out4(READ_ALU_LSR), .out5(READ_ALU_RL),
    .out6(READ_ALU_RR), .out7(READ_ALU_ADD), .out8(READ_ALU_SUB), .out9(READ_ALU_INCA),
    .out10(READ_ALU_INCX), .out11(READ_ALU_INCY), .out12(READ_ALU_INCP), .out13(READ_ALU_NOT),
    .out14(READ_ALU_DECP), .out15(MODE_SP), .in(1'b1), .sel(INS_Lookup_Table_data[3:0]));  // open: out0
  Demultiplexer #(.select(2)) demultiplexer_4 (
    .out1(demultiplexer_4_out1), .out2(demultiplexer_4_out2), .out3(demultiplexer_4_out3), .in(1'b1),
    .sel(INS_Lookup_Table_data[6:5]));  // open: out0
  buf buffer_17 (READ_X, demultiplexer_2_out1);
  buf buffer_18 (READ_Y, demultiplexer_2_out2);
  buf buffer_19 (READ_A, demultiplexer_2_out3);
  buf buffer_20 (READ_P, demultiplexer_2_out4);
  buf buffer_21 (READ_I, demultiplexer_2_out5);
  buf buffer_22 (READ_MEM, demultiplexer_2_out6);
  buf buffer_23 (READ_SP, demultiplexer_2_out7);
  buf buffer_24 (RESET_PC, demultiplexer_4_out1);
  buf buffer_25 (LOAD_PC, demultiplexer_4_out2);
  buf buffer_26 (PAUSE_PC, demultiplexer_4_out3);
  Demultiplexer #(.select(3)) demultiplexer_5 (
    .out1(demultiplexer_5_out1), .out2(demultiplexer_5_out2), .out3(demultiplexer_5_out3),
    .out4(demultiplexer_5_out4), .out5(demultiplexer_5_out5), .out6(demultiplexer_5_out6), .in(1'b1),
    .sel(INS_Lookup_Table_data[9:7]));  // open: out0, out7
  assign DATA_BUS_IN = ram_1_dout;  // Buffer buffer_27, 16 bits wide
  assign INS_REG = ram_1_dout;  // Buffer buffer_28, 16 bits wide
  buf buffer_29 (ADD_PAGE, demultiplexer_5_out1);
  buf buffer_30 (SUB_PAGE, demultiplexer_5_out2);
  buf buffer_31 (buffer_31_out, demultiplexer_5_out3);
  buf buffer_32 (INC_SP, demultiplexer_5_out4);
  buf buffer_33 (WRITE_MAR, demultiplexer_5_out5);
  buf buffer_34 (READ_MAR, demultiplexer_5_out6);
  // Probe on DATA_BUS_IN
  or or_6 (OUT_MODE, ADD_PAGE, READ_ALU_AND, READ_ALU_OR, READ_ALU_NOT, READ_ALU_LSL, READ_ALU_LSR, READ_ALU_RL, READ_ALU_RR, READ_ALU_ADD, READ_ALU_SUB, READ_SP, READ_ALU_INCA, READ_ALU_INCX, READ_ALU_INCY, READ_ALU_INCP, READ_X, READ_Y, READ_A, READ_P, READ_MAR, SUB_PAGE);
  Comparator #(.width(16)) comparator_4 (.a(INS_DECODER), .b(16'h5a1), .eq(comparator_4_eq));  // open: gt, lt
  Comparator #(.width(16)) comparator_5 (.a(INS_DECODER), .b(16'h5e1), .eq(comparator_5_eq));  // open: gt, lt
  Comparator #(.width(16)) comparator_6 (.a(INS_DECODER), .b(16'h621), .eq(comparator_6_eq));  // open: gt, lt
  or or_7 (or_7_out, comparator_4_eq, comparator_5_eq, comparator_6_eq);
  buf buffer_35 (COND_INS, or_7_out);

  // Other names for the same wires on the sheet: ZERO_FLAG = FLAG_REG_OUT[0]; FLAG_REG_OUT[1] = CARRY_FLAG;
  //   OVERFLOW_FLAG = FLAG_REG_OUT[2]; PARITY_FLAG = FLAG_REG_OUT[3]; NEGATIVE_FLAG = FLAG_REG_OUT[4]

  // Notes on the sheet:
  //   ALU
  //   Logical Shift Left
  //   Logical Shift Right
  //   Rotate Left
  //   Rotate Right
  //   Load PC Value
  //   Flag Checks
  //   Flag Comparison
  //   contents of INS_Lookup_Table (hex, n*v repeats v):
  //   10 7800 10 3800 10 5800 10 cc00 10 c400 10 c800 10 7801 10 7802 10 780d 10 7803 10 7804 10 7805 10
  //   7806 10 7809 10 380a 10 580b 10 980c 10 7807 10 7808 10 800e 10 1840 10 1040 10 c40 10 440 10 840 10
  //   280 1c40 c600 340 10 280 1c40 ca00 340 10 280 1c40 ce00 340 10 280 1c40 3a0f 340 10 280 1c40 5a0f
  //   340 10 280 1c40 7a0f 340 10 48*0 6680 1847 7800 340 10 6680 1847 3800 340 10 6680 1847 5800 340 10
  //   6680 1847 cc00 340 10 6680 1847 c400 340 10 6680 1847 c800 340 10 6680 1847 7801 340 10 6680 1847
  //   7802 340 10 6680 1847 7807 340 10 6680 1847 7808 340 10 6680 1847 1840 340 10 73*0 280 140 7800 340
  //   10 280 140 3800 340 10 280 140 5800 340 10 280 140 cc00 340 10 280 140 c400 340 10 280 140 c800 340
  //   10 280 140 7801 340 10 280 140 7802 340 10 280 140 7807 340 10 280 140 7808 340 10 280 140 1840 10
  //   202*0 280 1840 7800 340 10 280 1840 3800 340 10 280 1840 5800 340 10 280 1840 cc00 340 10 280 1840
  //   c400 340 10 280 1840 c800 340 10 280 1840 7801 340 10 280 1840 7802 340 10 280 1840 7807 340 10 280
  //   1840 7808 340 10 280 1840 1840 10 280 1840 c40 340 10 69*0 280 c0 7800 340 10 280 c0 3800 340 10 280
  //   c0 5800 340 10 280 c0 cc00 340 10 280 c c400 340 10 280 c0 c800 340 10 280 c0 7801 340 10 280 c0
  //   7802 340 10 280 c0 7807 340 10 280 c0 7808 340 10 280 c0 1840 10 74*0 6a80 1847 7800 340 10 6a80
  //   1847 3800 340 10 6a80 1847 5800 340 10 6a80 1847 cc00 340 10 6a80 1847 c400 340 10 6a80 1847 c800
  //   340 10 6a80 1847 7801 340 10 6a80 1847 7802 340 10 6a80 1847 7807 340 10 6a80 1847 7808 340 10 6a80
  //   1847 1840 10 124*0 1840 1840 10 78*0 10
  //   Instruction Decoder
  //   RAM
  //   Read Group
  //   Write Group
  //   ALU Group
  //   Program Counter Group
  //   Stack Pointer Group
endmodule
